# Fritzing sketch sketch (saved by Fritzing 0.9.2b)
circuit board: 8.46667cm x 5.64444cm

parts:
  Part2 = Arduino Nano (Rev3.0)
  RHT1 = Humidity and Temperature Sensor RHT03
  U1 = RELAY [package=relay-jzc]

nets:
  N1: Part2.GND, RHT1.GND_2, U1.MAIN
  N2: Part2.D2, RHT1.Data-signal
  N3: Part2.D4, U1.COIL1
  3V3: Part2.3V3, RHT1.Vcc
